# Fritzing sketch AutoTurntable (saved by Fritzing 0.9.9b)
breadboards: 3

parts:
  A1 = Arduino Nano (Rev3.0)
  J6 = shrouded pin header, 6 pins [form="♂ (shrouded male)"]
  J12 = shrouded pin header, 6 pins [form="♂ (shrouded male)"]
  JP1 = male pin header, 3 pins [form="♂ (male)"]
  J9 = shrouded pin header, 6 pins [form="♂ (shrouded male)"]
  C1 = Electrolytic Capacitor [capacitance=3.3µF voltage=50V package="100 mil [THT, electrolytic]"]
  J11 = shrouded pin header, 8 pins [form="♂ (shrouded male)"]
  D1 = Rectifier Diode [part_number=1N007 package="300 mil [THT]"]
  U2 = ADG333AB [chip_label=U package="DIP (Dual Inline) [THT]"]
  Q2 = Basic FET P-Channel [part_number=TIP120 package="TO220 [THT]"]
  U3 = ULN2003A [package="DIP16 [THT]"]
  U4 = ULN2003A [package="DIP16 [THT]"]
  P2 = POT [package=pot_alpha_rv16af-20]
  P3 = POT [package=pot_alpha_rv16af-20]
  P1 = POT [package=pot_alpha_rv16af-20]
  U1 = IC, DIP package, 28 pins [chip_label=IC]
  J29 = male pin header, 4 pins [form="♂ (male)"]
  J3 = male pin header, 3 pins [form="♂ (male)"]
  J4 = male pin header, 3 pins [form="♂ (male)"]
  J2 = male pin header, 3 pins [form="♂ (male)"]
  J14 = male pin header, 5 pins [form="♂ (male)"]
  J13 = male pin header, 5 pins [form="♂ (male)"]
  J20 = male pin header, 3 pins [form="♂ (male)"]
  J21 = male pin header, 3 pins [form="♂ (male)"]
  J22 = male pin header, 3 pins [form="♂ (male)"]
  J23 = male pin header, 3 pins [form="♂ (male)"]
  J24 = male pin header, 3 pins [form="♂ (male)"]
  J25 = male pin header, 3 pins [form="♂ (male)"]
  J26 = shrouded pin header, 16 pins [form="♂ (shrouded male)"]
  D3 = Rectifier Diode [part_number=1N007 package="300 mil [THT]"]
  D4 = Rectifier Diode [part_number=1N007 package="300 mil [THT]"]
  D6 = Rectifier Diode [part_number=1N007 package="300 mil [THT]"]
  J15 = male pin header, 2 pins [form="♂ (male)"]
  J16 = female pin header, 2 pins [form="♀ (female)"]
  J17 = female pin header, 2 pins [form="♀ (female)"]
  J18 = female pin header, 2 pins [form="♀ (female)"]
  J19 = female pin header, 2 pins [form="♀ (female)"]
  J30 = female pin header, 2 pins [form="♀ (female)"]
  D11 = Rectifier Diode [part_number=1N007 package="300 mil [THT]"]
  J1 = screw terminal, 2 pins
  J31 = screw terminal, 2 pins
  U7 = Voltage Regulator - Variable [package="TO220 [THT]"]
  Q3 = Basic FET P-Channel [part_number=TIP120 package="TO220 [THT]"]
  J32 = male pin header, 5 pins [form="♂ (male)"]
  J33 = male pin header, 3 pins [form="♂ (male)"]
  J34 = male pin header, 3 pins [form="♂ (male)"]
  D12 = Rectifier Diode [part_number=1N007 package="300 mil [THT]"]
  RL1 = DPDT Relay [chip_label=Relay package="DIP (Dual Inline) [THT]"]
  D13 = Rectifier Diode [part_number=1N007 package="300 mil [THT]"]
  Q4 = Basic FET P-Channel [part_number=TIP120 package="TO220 [THT]"]
  D14 = Rectifier Diode [part_number=1N007 package="300 mil [THT]"]
  D15 = Rectifier Diode [part_number=1N007 package="300 mil [THT]"]
  D16 = Rectifier Diode [part_number=1N007 package="300 mil [THT]"]
  D17 = Rectifier Diode [part_number=1N007 package="300 mil [THT]"]
  D5 = Rectifier Diode [part_number=1N007 package="300 mil [THT]"]
  R24 = Resistor [tolerance=±5% resistance=10k power=0.25 package="0603 [SMD]"]
  R18 = Resistor [tolerance=±5% resistance=10k power=0.25 package="0603 [SMD]"]
  R19 = Resistor [tolerance=±5% resistance=10k power=0.25 package="0603 [SMD]"]
  R20 = Resistor [tolerance=±5% resistance=10k power=0.25 package="0603 [SMD]"]
  C7 = Ceramic Capacitor [capacitance=1µF voltage=35V package="0603 [SMD, multilayer]"]
  R10 = Resistor [tolerance=±5% resistance=10k power=0.25 package="0603 [SMD]"]
  R12 = Resistor [tolerance=±5% resistance=10k power=0.25 package="0603 [SMD]"]
  R11 = Resistor [tolerance=±5% resistance=10k power=0.25 package="0603 [SMD]"]
  R9 = Resistor [tolerance=±5% resistance=10k power=0.25 package="0603 [SMD]"]
  C5 = Ceramic Capacitor [capacitance="100 nF" voltage=35V package="0603 [SMD, multilayer]"]
  C6 = Ceramic Capacitor [capacitance="100 nF" voltage=35V package="0603 [SMD, multilayer]"]
  C3 = Ceramic Capacitor [capacitance="100 nF" voltage=35V package="0603 [SMD, multilayer]"]
  C4 = Ceramic Capacitor [capacitance="100 nF" voltage=35V package="0603 [SMD, multilayer]"]
  R15 = Resistor [tolerance=±5% resistance=10k power=0.25 package="0603 [SMD]"]
  R25 = Resistor [tolerance=±5% resistance=10k power=0.25 package="0603 [SMD]"]
  R4 = Resistor [tolerance=±5% resistance=10k power=0.25 package="0603 [SMD]"]
  R5 = Resistor [tolerance=±5% resistance=10k power=0.25 package="0603 [SMD]"]
  R7 = Resistor [tolerance=±5% resistance=10k power=0.25 package="0603 [SMD]"]
  R13 = Resistor [tolerance=±5% resistance=10k power=0.25 package="0603 [SMD]"]
  R14 = Resistor [tolerance=±5% resistance=10k power=0.25 package="0603 [SMD]"]
  C10 = Ceramic Capacitor [capacitance="100 nF" voltage=35V package="0603 [SMD, multilayer]"]
  C9 = Ceramic Capacitor [capacitance="100 nF" voltage=35V package="0603 [SMD, multilayer]"]
  C8 = Ceramic Capacitor [capacitance="100 nF" voltage=35V package="0603 [SMD, multilayer]"]
  R23 = Resistor [tolerance=±5% resistance=1k power=0.25 package="0603 [SMD]"]
  C12 = Ceramic Capacitor [capacitance=10µF voltage=35V package="0603 [SMD, multilayer]"]
  R8 = Resistor [tolerance=±5% resistance=1k power=0.25 package="0603 [SMD]"]
  U8 = 74AHC1G08 [package=sot23-5]
  C13 = Ceramic Capacitor [capacitance="100 nF" voltage=35V package="0603 [SMD, multilayer]"]
  U5 = TC7SU04F [package=sot23-5]
  C11 = Ceramic Capacitor [capacitance="100 nF" voltage=35V package="0603 [SMD, multilayer]"]
  R28 = Resistor [tolerance=±5% resistance=1k power=0.25 package="0603 [SMD]"]
  R27 = Resistor [tolerance=±5% resistance=10k power=0.25 package="0603 [SMD]"]
  R26 = Resistor [tolerance=±5% resistance=10k power=0.25 package="0603 [SMD]"]

nets:
  N1: A1.D1/TX, J25.pin1
  GND: A1.GND, C1.-, U2.VSS, U2.GND, Q2.source, U3.0V, U4.0V, U1.pin12, U1.pin27, J29.pin2, J3.pin1, J3.pin2, J3.pin3, J20.pin3, J21.pin3, J22.pin3, J23.pin3, J24.pin3, J25.pin3, J26.pin16, J1.pin2, J31.pin2, U7.GND, Q3.source, Q4.source, R24.Pin_0, R18.Pin_0, R19.Pin_0, R20.Pin_0, C7.1, R10.Pin_1, R12.Pin_1, R11.Pin_1, R9.Pin_1, C5.0, C6.1, C3.0, C4.1, R15.Pin_0, R25.Pin_1, R4.Pin_1, R5.Pin_1, R7.Pin_1, R13.Pin_0, R14.Pin_0, C9.0, C8.0, C12.1, U8.GND, C13.1, U5.GND, C11.1, R27.Pin_0, R26.Pin_0
  N2: A1.D2, U1.pin17
  N3: A1.D3, U1.pin16
  N4: A1.D4, U1.pin15
  N5: A1.D5, U1.pin14
  N6: A1.D6, U1.pin28
  N7: A1.D7, U2.D1
  N8: A1.D8, U2.D2
  N9: A1.D9, U2.D3
  N10: A1.D10, U2.D4
  N11: A1.D11/MOSI, U2.IN1, U2.IN2, U2.IN3, U2.IN4
  N12: A1.D12/MISO, J11.pin4, J26.pin5
  VIN: A1.VIN, J6.pin1, J6.pin3, J12.pin2, J12.pin5, JP1.pin2, J9.pin2, J9.pin5, C1.+, J11.pin1, U2.VDD, U3.COM_-_Common, U4.COM_-_Common, P2.A, P3.A, P1.A, U1.pin1, U1.pin18, J29.pin1, J2.pin1, J2.pin2, J2.pin3, J14.pin1, J13.pin1, J20.pin2, J21.pin2, J22.pin2, J23.pin2, J24.pin2, J25.pin2, J26.pin1, D6.anode, J16.pin1, J17.pin1, J30.pin2, RL1.pin8, D5.anode, C7.0, C5.1, C6.0, C3.1, C4.0, C10.0, C9.1, C8.1, U8.VCC, C13.0, U5.+V, C11.0
  N13: A1.A7, R8.Pin_0
  N14: A1.A5, J29.pin4
  N15: A1.A4, J29.pin3
  N16: A1.A2, P3.S
  N17: A1.A1, P2.S
  N18: A1.A0, P1.S
  N19: A1.3V3, J4.pin1, J4.pin2, J4.pin3
  N20: A1.D13/SCK, J11.pin3, J26.pin6
  N21: J6.pin2, J6.pin5, D11.cathode
  N22: J6.pin6, U1.pin8, J26.pin14, R15.Pin_1
  N23: J12.pin4, JP1.pin3, U1.pin10, R14.Pin_1
  N24: J12.pin6, JP1.pin1, U1.pin11, R13.Pin_1
  N25: J9.pin1, J9.pin3, J26.pin7, D16.anode
  N26: J9.pin6, U1.pin5, D14.anode, R25.Pin_0
  N27: J11.pin5, R4.Pin_0
  N28: J11.pin6, R5.Pin_0
  N29: J11.pin8, R7.Pin_0
  N30: D1.cathode, J15.pin1, U7.OUT, C12.0
  N31: D1.anode, Q2.drain, J15.pin2
  N32: U2.S1A, U4.In_1
  N33: U2.S1B, U3.In_1
  N34: U2.S2B, U3.In_2
  N35: U2.S2A, U4.In_2
  N36: U2.S3A, U4.In_3
  N37: U2.S3B, U3.In_3
  N38: U2.S4B, U3.In_4
  N39: U2.S4A, U4.In_4
  N40: Q2.gate, R8.Pin_1
  N41: U3.Out_4, J13.pin5
  N42: U3.Out_3, J13.pin4
  N43: U3.Out_2, J13.pin3
  N44: U3.Out_1, J13.pin2
  N45: U4.Out_4, J14.pin5
  N46: U4.Out_3, J14.pin4
  N47: U4.Out_2, J14.pin3
  N48: U4.Out_1, J14.pin2
  N49: P2.E, R19.Pin_1
  N50: P3.E, R18.Pin_1
  N51: P1.E, R20.Pin_1
  N52: U1.pin6, J30.pin1, R24.Pin_1
  N53: U1.pin9, J24.pin1
  N54: U1.pin19, J16.pin2, R9.Pin_0
  N55: U1.pin20, J17.pin2, R10.Pin_0
  N56: U1.pin21, D4.cathode, J18.pin2, R11.Pin_0
  N57: U1.pin22, D3.cathode, J19.pin2, R12.Pin_0
  N58: U1.pin23, J20.pin1
  N59: U1.pin24, J21.pin1
  N60: U1.pin25, J22.pin1
  N61: U1.pin26, J23.pin1, J26.pin2, U5.IN
  N62: J26.pin3, D3.anode
  N63: J26.pin4, D4.anode
  N64: J26.pin8, D15.anode
  N65: J26.pin9, D17.anode
  N66: D6.cathode, J19.pin1
  N67: J18.pin1, D5.cathode
  N68: D11.anode, J1.pin1
  N69: J31.pin1, D12.anode
  N70: U7.IN, J33.pin2, J34.pin2, D12.cathode
  N71: Q3.gate, R23.Pin_1
  N72: Q3.drain, J32.pin5, D13.anode
  N73: J32.pin2, J32.pin3
  N74: J32.pin4, RL1.pin7, D13.cathode
  N75: J33.pin1, RL1.pin5
  N76: J33.pin3, R26.Pin_1
  N77: J34.pin1, RL1.pin6
  N78: J34.pin3, R27.Pin_1
  N79: RL1.pin1, Q4.drain
  N80: Q4.gate, R28.Pin_1
  N81: D14.cathode, D15.cathode, R28.Pin_0
  N82: D16.cathode, D17.cathode, U8.B
  N83: R23.Pin_0, U8.Y
  N84: U8.A, U5.OUT

notes:
  Power SW
  5v DC in
  Speed SW
  Size SW
  Size Jumper
  12" Play Sensor
  LEDs
  PW SW
  SZ SW
  7-Seg Disp.
  Solenoid
  7S DISP
  SOl
  7"
  12"
  NC = 10"
  Vertical Motor
  Horiz. Motor
  [
  Upper Limit
  Lower Limit
  V MTR
  H MTR
  Pause Button
  Play/Home Button
  U LIM
  L LIM
  PA BT
  PL BT
  7" Play Sensor
  10" Play Sensor
  Home Sensor
  10"
  HOME
  Pickup Sensor
  Speed Sensor
  5v DC
  3.3v DC
  GND
  SPEED
  PICKUP
  7" Cal Pot
  10" Cal Pot
  12" Cal Pot
  5v DC In
  +
  -
  33-RPM Pot
  45-RPM Pot
  33 POT
  45 POT
  TURN MTR
  SPD SW
  7" CAL
  10" CAL
  12" CAL
  Automatic Changer Comm
  _
  +5v
  Mux S16
  Mux S15
  Auto-mode indicator (Mux S12)
  5v DC out
  NC
  Turntable power indicator LED
  33-RPM pot
  J12 pin 2
  45-RPM pot
  J12 pin 3
  J12 pin 4
  Q3 drain
  J10 pin 5
  Power indicator LED (5v)
  Turntable power indicator LED (J10 pin 3)
  Pause status LED (Ard. D13)
  Play status LED (Ard. D12)
  Play status LED GND
  Pause status LED GND
  Turntable power indicator LED GND
  Power indicator LED GND
  SW 1
  SW 2
  SW 3
  SW 4
  SW 5
  SW 6
  5v
  HOME ST
  AUT ST
  PAUSE CMD
  PLAY CMD
  PLAY ST
  PAUSE ST
  SPEED SW ST
  Automatic Record Player
  Version 0.2 (Jan 2022)
  Designed by Patrick Nelson
  github.com/pdnelson
  Calibration Display Button
  CAL
  12v DC in
  Turn Motor
  SPEED SET
  TURN PWR
  12v DC In

custom parts:
  ADG333AB: A DIP stand-in part for whatever IC you want. With 20 pins on a 300mil dual inline package (DIP) footprint.
  Voltage Regulator - Variable: Variable DC Voltage Regulator
  DPDT Relay: DIP DPDT Relay (Double Pole Double Throw)
