# Fritzing sketch AudioPassController (saved by Fritzing 0.9.9b)
circuit board: 5.47685cm x 1.7891cm

parts:
  J1 = male pin header, 3 pins [form="♂ (male)"]
  J3 = male pin header, 2 pins [form="♂ (male)"]
  J4 = male pin header, 2 pins [form="♂ (male)"]
  J2 = screw terminal, 4 pins
  C3 = Ceramic Capacitor [capacitance=47nF voltage=35V package="0805 [SMD, multilayer]"]
  R1 = Resistor [tolerance=±5% resistance=10k power=0.25 package="0603 [SMD]"]
  R2 = Resistor [tolerance=±5% resistance=10k power=0.25 package="0603 [SMD]"]
  C2 = Ceramic Capacitor [capacitance=1µF voltage=35V package="0805 [SMD, multilayer]"]
  C1 = Ceramic Capacitor [capacitance=10µF voltage=35V package="0805 [SMD, multilayer]"]
  C4 = Ceramic Capacitor [capacitance="100 nF" voltage=35V package="0603 [SMD, multilayer]"]
  C5 = Ceramic Capacitor [capacitance="100 nF" voltage=35V package="0603 [SMD, multilayer]"]
  U2 = SN74LVC2G14DBVR [package=SOT23-6]
  U1 = SN74LVC2G14DBVR [package=SOT23-6]

nets:
  N1: J1.pin1, U2.SELECT, U1.SELECT
  VCC: J1.pin2, C3.0, C2.0, C1.0, C4.1, C5.1, U2.VCC, U1.VCC
  GND: J1.pin3, C3.1, C2.1, C1.1, C4.0, C5.0, U2.GND, U1.GND
  N2: J3.pin1, U1.COM
  N3: J3.pin2, J2.pin2, R1.Pin_0
  N4: J4.pin1, U2.COM
  N5: J4.pin2, J2.pin4, R2.Pin_0
  N6: J2.pin1, U1.1Y
  N7: J2.pin3, U2.1Y
  N8: R1.Pin_1, U1.2Y
  N9: R2.Pin_1, U2.2Y

notes:
  AUDIO OFF
  GND
  5v
  pause or play command is active
  Relay to disable audio when
  Output
  Input
  L+ (White)
  L- (Blue)
  R+ (Red)
  R- (Green)
  L
  +  -
  R
  White
  Blue
  Red
  Green
  Auto-Turntable
  +
  -
  COM
  _
  Audio Controller
  v0.1 (Dec 2022)

custom parts:
  SN74LVC2G14DBVR: This dual Schmitt-trigger inverter is designed for 1.65-V to 5.5-V VCC operation. The SN74LVC2G14 contains two inverters and performs the Boolean function Y = A. The device functions as two independent inverters, but because of Schmitt action, it may have different input threshold levels for positive-going (VT+) and negative-going (VT–) signals. This device is fully specified for partial-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
