# Fritzing sketch AutoTurntable (saved by Fritzing 0.9.9b)
circuit board: 8cm x 17.4cm
breadboards: 3

parts:
  A1 = Arduino Nano (Rev3.0)
  J3 = shrouded pin header, 6 pins [form="♂ (shrouded male)"]
  J4 = shrouded pin header, 6 pins [form="♂ (shrouded male)"]
  J28 = shrouded pin header, 8 pins [form="♂ (shrouded male)"]
  U3 = ULN2003A [package="DIP16 [THT]"]
  U2 = ULN2003A [package="DIP16 [THT]"]
  J2 = male pin header, 4 pins [form="♂ (male)"]
  J10 = male pin header, 5 pins [form="♂ (male)"]
  J11 = male pin header, 5 pins [form="♂ (male)"]
  J24 = male pin header, 3 pins [form="♂ (male)"]
  J26 = male pin header, 3 pins [form="♂ (male)"]
  J25 = male pin header, 3 pins [form="♂ (male)"]
  J19 = shrouded pin header, 16 pins [form="♂ (shrouded male)"]
  D10 = Rectifier Diode [part_number=1N007 package="300 mil [THT]"]
  D11 = Rectifier Diode [part_number=1N007 package="300 mil [THT]"]
  D8 = Rectifier Diode [part_number=1N007 package="300 mil [THT]"]
  J1 = screw terminal, 2 pins
  Q2 = Basic FET P-Channel [part_number=TIP120 package="TO220 [THT]"]
  J5 = male pin header, 3 pins [form="♂ (male)"]
  J6 = male pin header, 3 pins [form="♂ (male)"]
  D2 = Rectifier Diode [part_number=1N007 package="300 mil [THT]"]
  D3 = Rectifier Diode [part_number=1N007 package="300 mil [THT]"]
  D6 = Rectifier Diode [part_number=1N007 package="300 mil [THT]"]
  D7 = Rectifier Diode [part_number=1N007 package="300 mil [THT]"]
  D9 = Rectifier Diode [part_number=1N007 package="300 mil [THT]"]
  R20 = Resistor [tolerance=±5% resistance=10k power=0.25 package="0603 [SMD]"]
  R24 = Resistor [tolerance=±5% resistance=10k power=0.25 package="0603 [SMD]"]
  R22 = Resistor [tolerance=±5% resistance=10k power=0.25 package="0603 [SMD]"]
  R25 = Resistor [tolerance=±5% resistance=10k power=0.25 package="0603 [SMD]"]
  R23 = Resistor [tolerance=±5% resistance=10k power=0.25 package="0603 [SMD]"]
  C6 = Ceramic Capacitor [capacitance="100 nF" voltage=35V package="0603 [SMD, multilayer]"]
  C7 = Ceramic Capacitor [capacitance="100 nF" voltage=35V package="0603 [SMD, multilayer]"]
  C8 = Ceramic Capacitor [capacitance="100 nF" voltage=35V package="0603 [SMD, multilayer]"]
  R19 = Resistor [tolerance=±5% resistance=10k power=0.25 package="0603 [SMD]"]
  R12 = Resistor [tolerance=±5% resistance=10k power=0.25 package="0603 [SMD]"]
  R13 = Resistor [tolerance=±5% resistance=1k power=0.25 package="0603 [SMD]"]
  R14 = Resistor [tolerance=±5% resistance=1k power=0.25 package="0603 [SMD]"]
  R21 = Resistor [tolerance=±5% resistance=10k power=0.25 package="0603 [SMD]"]
  R18 = Resistor [tolerance=±5% resistance=10k power=0.25 package="0603 [SMD]"]
  R6 = Resistor [tolerance=±5% resistance=1k power=0.25 package="0603 [SMD]"]
  U7 = 74AHC1G08 [package=sot23-5]
  C3 = Ceramic Capacitor [capacitance="100 nF" voltage=35V package="0603 [SMD, multilayer]"]
  R9 = Resistor [tolerance=±5% resistance=10k power=0.25 package="0603 [SMD]"]
  R8 = Resistor [tolerance=±5% resistance=10k power=0.25 package="0603 [SMD]"]
  C5 = Ceramic Capacitor [capacitance="100 nF" voltage=35V package="0603 [SMD, multilayer]"]
  J16 = male pin header, 2 pins [form="♂ (male)"]
  J17 = male pin header, 2 pins [form="♂ (male)"]
  J14 = male pin header, 2 pins [form="♂ (male)"]
  J15 = male pin header, 2 pins [form="♂ (male)"]
  J12 = male pin header, 2 pins [form="♂ (male)"]
  C14 = Ceramic Capacitor [capacitance=1µF voltage=35V package="0805 [SMD, multilayer]"]
  U1 = Voltage Regulator - Variable [package="TO220 [THT]"]
  C4 = Ceramic Capacitor [capacitance=10µF voltage=35V package="0805 [SMD, multilayer]"]
  R11 = Resistor [tolerance=±5% resistance=10k power=0.25 package="0603 [SMD]"]
  C9 = Ceramic Capacitor [capacitance="100 nF" voltage=35V package="0603 [SMD, multilayer]"]
  C10 = Ceramic Capacitor [capacitance="100 nF" voltage=35V package="0603 [SMD, multilayer]"]
  C11 = Ceramic Capacitor [capacitance="100 nF" voltage=35V package="0603 [SMD, multilayer]"]
  C12 = Ceramic Capacitor [capacitance="100 nF" voltage=35V package="0603 [SMD, multilayer]"]
  U11 = SN74LVC1G18DBVR [package=sot-23-6]
  U10 = SN74LVC1G18DBVR [package=sot-23-6]
  U9 = SN74LVC1G18DBVR [package=sot-23-6]
  U8 = SN74LVC1G18DBVR [package=sot-23-6]
  R5 = Resistor [tolerance=±5% resistance=10k power=0.25 package="0603 [SMD]"]
  D1 = Rectifier Diode [part_number=1N007 package="300 mil [THT]"]
  J18 = male pin header, 3 pins [form="♂ (male)"]
  J27 = male pin header, 3 pins [form="♂ (male)"]
  U5 = CD4051BE 8-channel mux [chip_label=IC package="DIP (Dual Inline) [THT]"]
  J13 = male pin header, 2 pins [form="♂ (male)"]
  U4 = MX1508 Motor Driver [chip_label=SOIC18-W package=SO]
  C2 = Capacitor Polarized [package=panasonic_d]
  R4 = Resistor [tolerance=±5% resistance=220 package="0805 [SMD]"]
  C1 = Capacitor Polarized [package=panasonic_d]
  RL1 = DPDT Relay [chip_label=Relay package="DIP (Dual Inline) [THT]"]
  J9 = male pin header, 2 pins [form="♂ (male)"]
  Q1 = Basic FET P-Channel [part_number=TIP120 package="TO220 [THT]"]
  R10 = Resistor [tolerance=±5% resistance=1k power=0.25 package="0603 [SMD]"]
  D5 = Rectifier Diode [part_number=1N007 package="300 mil [THT]"]
  l = male pin header, 1 pin [form="♂ (male)"]
  R1 = male pin header, 1 pin [form="♂ (male)"]
  D4 = Rectifier Diode [part_number=1N007 package="300 mil [THT]"]
  l_2 = male pin header, 1 pin [form="♂ (male)"]
  R3 = male pin header, 1 pin [form="♂ (male)"]
  l_3 = male pin header, 1 pin [form="♂ (male)"]
  R2 = male pin header, 1 pin [form="♂ (male)"]
  U6 = Voltage Regulator - Variable [package="TO220 [THT]"]
  R16 = Resistor [tolerance=±5% resistance=10k power=0.25 package="0603 [SMD]"]
  C13 = Ceramic Capacitor [capacitance=10µF voltage=35V package="0805 [SMD, multilayer]"]
  J21 = screw terminal, 2 pins
  RL2 = DPDT Relay [chip_label=Relay package="DIP (Dual Inline) [THT]"]
  J20 = male pin header, 2 pins [form="♂ (male)"]
  D12 = Rectifier Diode [part_number=1N007 package="300 mil [THT]"]
  Q3 = Basic FET P-Channel [part_number=TIP120 package="TO220 [THT]"]
  R17 = Resistor [tolerance=±5% resistance=10k power=0.25 package="0603 [SMD]"]
  D16 = Diode [package=sma-diode-kit]
  RL3 = DPDT Relay [chip_label=Relay package="DIP (Dual Inline) [THT]"]
  D13 = Rectifier Diode [part_number=1N007 package="300 mil [THT]"]
  Q4 = Basic FET P-Channel [part_number=TIP120 package="TO220 [THT]"]
  R15 = Resistor [tolerance=±5% resistance=1k power=0.25 package="0603 [SMD]"]
  J23 = male pin header, 2 pins [form="♂ (male)"]
  J22 = male pin header, 2 pins [form="♂ (male)"]
  D15 = Rectifier Diode [part_number=1N007 package="300 mil [THT]"]
  D14 = Rectifier Diode [part_number=1N007 package="300 mil [THT]"]
  R41 = Resistor [tolerance=±5% resistance=1k power=0.25 package="0603 [SMD]"]
  RL4 = DPDT Relay [chip_label=Relay package="DIP (Dual Inline) [THT]"]
  D17 = Rectifier Diode [part_number=1N007 package="300 mil [THT]"]
  Q5 = Basic FET P-Channel [part_number=TIP120 package="TO220 [THT]"]
  J8 = male pin header, 3 pins [form="♂ (male)"]
  R42 = Resistor [tolerance=±5% resistance=10k power=0.25 package="0603 [SMD]"]
  J7 = male pin header, 3 pins [form="♂ (male)"]
  R43 = Resistor [tolerance=±5% resistance=10k power=0.25 package="0603 [SMD]"]
  D18 = Rectifier Diode [part_number=1N007 package="300 mil [THT]"]
  D19 = Rectifier Diode [part_number=1N007 package="300 mil [THT]"]
  R44 = Resistor [tolerance=±5% resistance=1k power=0.25 package="0603 [SMD]"]
  J34 = male pin header, 2 pins [form="♂ (male)"]

nets:
  GND: A1.GND, U3.0V, U2.0V, J2.pin2, J24.pin3, J26.pin3, J25.pin3, J19.pin16, J1.pin2, Q2.source, R20.Pin_0, R24.Pin_1, R22.Pin_1, R25.Pin_1, R23.Pin_1, C6.1, C7.0, C8.1, R19.Pin_0, R12.Pin_1, R13.Pin_1, R14.Pin_1, R21.Pin_0, R18.Pin_0, U7.GND, C3.1, R9.Pin_0, R8.Pin_0, C5.1, C14.1, U1.GND, C4.1, R11.Pin_1, C9.0, C10.0, C11.1, C12.1, U11.GND, U10.GND, U9.GND, U8.GND, R5.Pin_1, J27.pin3, U5.Negative, U5.Ground, U4.idk_(connect_to_ground), C2.-, C1.-, Q1.source, U6.GND, R16.Pin_1, C13.1, Q3.source, R17.Pin_0, D16.A, Q4.source, Q5.source, R42.Pin_0, R43.Pin_0
  N1: A1.D2, U5.Selector_A
  N2: A1.D3, U5.Selector_B
  N3: A1.D4, U5.Selector_C
  N4: A1.D6, U5.COM_I/O
  N5: A1.D7, U8.A
  N6: A1.D8, U9.A
  N7: A1.D9, U10.A
  N8: A1.D10, U11.S, U10.S, U9.S, U8.S
  N9: A1.D11/MOSI, U11.A
  N10: A1.D12/MISO, U4.Motor_1_logic_1
  VDD: A1.VIN, J3.pin5, J4.pin2, J4.pin5, J28.pin1, U3.COM_-_Common, U2.COM_-_Common, J2.pin1, J10.pin1, J11.pin1, J24.pin2, J26.pin2, J25.pin2, J19.pin2, D8.anode, D9.anode, C6.0, C7.1, C8.0, U7.VCC, C3.0, C5.0, J14.pin1, J15.pin1, J12.pin2, C14.0, U1.OUT, C4.0, R11.Pin_0, C9.1, C10.1, C11.0, C12.0, U11.VDD, U10.VDD, U9.VDD, U8.VDD, J18.pin2, J27.pin2, U5.5v_input
  N11: A1.A7, J27.pin1
  N12: A1.A6, J26.pin1
  N13: A1.A5, J2.pin4
  N14: A1.A4, J2.pin3
  N15: A1.A3, J25.pin1
  N16: A1.A2, J24.pin1, J19.pin1, U7.A
  N17: A1.A1, U4.Motor_1_logic_2
  N18: A1.A0, J28.pin4, J19.pin5, D15.anode
  N19: A1.D13/SCK, J28.pin3, J19.pin6, D14.anode
  N20: J3.pin1, J3.pin3, J5.pin2, J6.pin2, U1.IN, U6.IN, J8.pin2, J7.pin2
  N21: J3.pin2, D1.cathode
  N22: J3.pin6, J19.pin14, R18.Pin_1, U5.Ch_5
  N23: J4.pin1, J4.pin3, J19.pin7, D6.anode
  N24: J4.pin6, D2.anode
  N25: J28.pin5, R12.Pin_0
  N26: J28.pin6, R13.Pin_0
  N27: J28.pin8, R14.Pin_0
  N28: U3.In_1, U11.Y1
  N29: U3.In_2, U10.Y1
  N30: U3.In_3, U9.Y1
  N31: U3.In_4, U8.Y1
  N32: U3.Out_4, J11.pin5
  N33: U3.Out_3, J11.pin4
  N34: U3.Out_2, J11.pin3
  N35: U3.Out_1, J11.pin2
  N36: U2.In_1, U11.Y0
  N37: U2.In_2, U10.Y0
  N38: U2.In_3, U9.Y0
  N39: U2.In_4, U8.Y0
  N40: U2.Out_4, J10.pin5
  N41: U2.Out_3, J10.pin4
  N42: U2.Out_2, J10.pin3
  N43: U2.Out_1, J10.pin2
  N44: J19.pin3, D10.anode
  N45: J19.pin4, D11.anode
  N46: J19.pin8, D3.anode
  N47: J19.pin9, D7.anode
  N48: J19.pin10, R19.Pin_1, J18.pin3, U5.Ch_7
  N49: J19.pin11, R21.Pin_1, J18.pin1, U5.Ch_4
  N50: J19.pin12, D18.anode
  N51: J19.pin13, D19.anode, J34.pin2
  N52: D10.cathode, R24.Pin_0, J17.pin2, U5.Ch_1
  N53: D11.cathode, R25.Pin_0, J16.pin2, U5.Ch_2
  N54: D8.cathode, J17.pin1
  N55: J1.pin1, D1.anode
  N56: Q2.gate, R6.Pin_1, Q3.gate
  N57: Q2.drain, J9.pin2, D4.anode
  N58: J5.pin1, l.pin1
  N59: J5.pin3, R8.Pin_1
  N60: J6.pin1, l_2.pin1
  N61: J6.pin3, R9.Pin_1
  N62: D2.cathode, D3.cathode, R10.Pin_0
  N63: D6.cathode, D7.cathode, U7.B, R5.Pin_0
  N64: D9.cathode, J16.pin1
  N65: R20.Pin_1, J12.pin1, U5.Ch_6
  N66: R22.Pin_0, J15.pin2, U5.Ch_3
  N67: R23.Pin_0, J14.pin2, U5.Ch_0
  N68: R6.Pin_0, U7.Y
  N69: U5.Disable_channels, R17.Pin_1
  N70: J13.pin1, U4.Motor_1_out_2
  N71: J13.pin2, U4.Motor_1_out_1
  N72: U4.VCC1, U4.VCC2, R4.Pin_1, C1.+, D16.C
  N73: U4.+5v_(VDD2_-_use_this_one), C2.+, R4.Pin_0, RL1.pin8, D5.cathode, U6.OUT, R16.Pin_0, C13.0, RL2.pin8, D12.cathode, RL3.pin8, D13.cathode, J34.pin1
  N74: RL1.pin1, Q1.drain, D5.anode
  N75: RL1.pin5, RL4.pin7
  N76: RL1.pin6, RL4.pin2
  N77: RL1.pin7, J9.pin1, D4.cathode
  N78: Q1.gate, R10.Pin_1
  N79: R1.pin1, RL4.pin6
  N80: R3.pin1, RL4.pin3
  N81: l_3.pin1, J7.pin1
  N82: R2.pin1, RL4.pin5
  N83: J21.pin1, RL2.pin7
  N84: J21.pin2, J20.pin1
  N85: RL2.pin1, D12.anode, Q3.drain
  N86: RL2.pin5, R41.Pin_1
  N87: J20.pin2, R41.Pin_0
  N88: RL3.pin1, D13.anode, Q4.drain
  N89: RL3.pin2, J23.pin2
  N90: RL3.pin3, J22.pin2
  N91: RL3.pin6, J22.pin1
  N92: RL3.pin7, J23.pin1
  N93: Q4.gate, R15.Pin_1
  N94: R15.Pin_0, D15.cathode, D14.cathode
  N95: RL4.pin1, D17.anode, Q5.drain
  N96: RL4.pin4, J8.pin1
  N97: RL4.pin8, D17.cathode
  N98: Q5.gate, R44.Pin_0
  N99: J8.pin3, R42.Pin_1
  N100: J7.pin3, R43.Pin_1
  N101: D18.cathode, D19.cathode, R44.Pin_1

notes:
  Power SW
  Speed SW
  Size SW
  LEDs
  PW SW
  SZ SW
  7-Seg Disp.
  7S DISP
  Vertical Motor
  Horiz. Motor
  [
  Upper Limit
  Lower Limit
  V MTR
  H MTR
  Pause Button
  Play/Home Button
  U LIM
  L LIM
  PA BT
  PL BT
  Home Sensor
  HOME
  Pickup Sensor
  Speed Sensor
  SPEED
  PICKUP
  33-RPM Pot
  45-RPM Pot
  33 POT
  45 POT
  TURN MTR
  SPD SW
  Automatic Changer Comm
  _
  GND
  +5v
  5v DC
  3.3v DC
  Mux S16
  Mux S15
  Auto-mode indicator (Mux S12)
  5v DC in
  5v DC out
  NC
  Turntable power indicator LED
  33-RPM pot
  J12 pin 2
  45-RPM pot
  J12 pin 3
  J12 pin 4
  Q3 drain
  J10 pin 5
  Power indicator LED (5v)
  Turntable power indicator LED (J10 pin 3)
  Pause status LED (Ard. D13)
  Play status LED (Ard. D12)
  Play status LED GND
  Pause status LED GND
  Turntable power indicator LED GND
  Power indicator LED GND
  SW 1
  SW 2
  SW 3
  SW 4
  SW 5
  SW 6
  1
  Automatic Record Player v0.4 (September 2022)
  Designed by Patrick Nelson (github.com/pdnelson)
  Calibration  Button
  CAL
  12v DC in
  12v DC
  -
  +
  Main 5v circuit
  ]
  Pickup Sensor Direction
  Horizontal Engagement Motor Controller
  Horizontal Engagement Motor
  Turn Motor
  33 RPM resistor
  45 RPM resistor
  16 RPM resistor
  6.3v AC in
  Strobe LEDs
  HG MTR
  PICKUP D
  16
  Audio in
  Audio out
  Relay to disable audio when
  pause or play command is active
  L-R O
  L-R I
  6.3v AC
  STRB
  78-RPM Pot
  16-RPM Pot
  Alt. Speed Button
  16 POT
  78 POT
  SPD ALT

custom parts:
  Voltage Regulator - Variable: Variable DC Voltage Regulator
  CD4051BE 8-channel mux: A DIP stand-in part for whatever IC you want. With 16 pins on a 300mil dual inline package (DIP) footprint.
  DPDT Relay: DIP DPDT Relay (Double Pole Double Throw)
