# Fritzing sketch StrobeController (saved by Fritzing 0.9.9b)
circuit board: 2.23583cm x 5.22174cm

parts:
  J3 = male pin header, 3 pins [form="♂ (male)"]
  RL1 = DPDT Relay [chip_label=Relay package="DIP (Dual Inline) [THT]"]
  J2 = male pin header, 2 pins [form="♂ (male)"]
  J1 = screw terminal, 2 pins
  R1 = Resistor [tolerance=±5% resistance=1k power=0.25 package="0603 [SMD]"]
  D1 = Rectifier Diode [part_number=1N007 package="300 mil [THT]"]
  R2 = Resistor [tolerance=±5% resistance=1k power=0.25 package="0603 [SMD]"]
  Q1 = Basic FET P-Channel [part_number=TIP120 package="TO220 [THT]"]
  C1 = Ceramic Capacitor [capacitance=0.47nF voltage=16V package="0805 [SMD, multilayer]"]

nets:
  N1: J3.pin1, R2.Pin_0
  N2: J3.pin2, RL1.pin8, D1.cathode, C1.1
  N3: J3.pin3, Q1.source
  N4: RL1.pin1, D1.anode, Q1.drain, C1.0
  N5: RL1.pin5, R1.Pin_1
  N6: RL1.pin7, J1.pin1
  N7: J2.pin1, J1.pin2
  N8: J2.pin2, R1.Pin_0
  N9: R2.Pin_1, Q1.gate

notes:
  Strobe LEDs
  6.3v AC in
  Comm
  _
  Strobe Controller Board v0.1 (Nov 2022)
  Automatic Record Player
  6.3v AC
  STRB

custom parts:
  DPDT Relay: DIP DPDT Relay (Double Pole Double Throw)
