# Fritzing sketch TurntableMotorController (saved by Fritzing 0.9.9b)
circuit board: 5.9cm x 7.5cm

parts:
  J5 = male pin header, 5 pins [form="♂ (male)"]
  RL1 = DPDT Relay [chip_label=Relay package="DIP (Dual Inline) [THT]"]
  Q1 = Basic FET P-Channel [part_number=TIP120 package="TO220 [THT]"]
  U1 = Voltage Regulator - Variable [package="TO220 [THT]"]
  D1 = Rectifier Diode [part_number=1N007 package="300 mil [THT]"]
  C3 = Ceramic Capacitor [capacitance=10µF voltage=35V package="0805 [SMD, multilayer]"]
  R14 = Resistor [tolerance=±5% resistance=1k power=0.25 package="0603 [SMD]"]
  R13 = Resistor [tolerance=±5% resistance=10k power=0.25 package="0603 [SMD]"]
  C4 = Ceramic Capacitor [capacitance=0.47nF voltage=16V package="0805 [SMD, multilayer]"]
  U2 = V_REG_LD1085 [package=d2pack_a]
  R1 = male pin header, 3 pins [form="♂ (male)"]
  R2 = male pin header, 3 pins [form="♂ (male)"]
  R3 = male pin header, 3 pins [form="♂ (male)"]
  R4 = male pin header, 3 pins [form="♂ (male)"]
  R11 = Resistor [tolerance=±5% resistance=104k power=0.25 package="0603 [SMD]"]
  R9 = Resistor [tolerance=±5% resistance=47k power=0.25 package="0603 [SMD]"]
  R7 = Resistor [tolerance=±5% resistance=26.7k power=0.25 package="0603 [SMD]"]
  R5 = Resistor [tolerance=±5% resistance=1k power=0.25 package="0603 [SMD]"]
  R12 = Resistor [tolerance=±5% resistance=94k power=0.25 package="0603 [SMD]"]
  R10 = Resistor [tolerance=±5% resistance=69k power=0.25 package="0603 [SMD]"]
  R8 = Resistor [tolerance=±5% resistance=47k power=0.25 package="0603 [SMD]"]
  R6 = Resistor [tolerance=±5% resistance=69k power=0.25 package="0603 [SMD]"]
  J3 = male pin header, 1 pin [form="♂ (male)"]
  J3_2 = male pin header, 1 pin [form="♂ (male)"]
  J4 = male pin header, 1 pin [form="♂ (male)"]
  J4_2 = male pin header, 1 pin [form="♂ (male)"]
  J4_3 = male pin header, 1 pin [form="♂ (male)"]
  J4_4 = male pin header, 1 pin [form="♂ (male)"]
  J3_3 = male pin header, 1 pin [form="♂ (male)"]
  J3_4 = male pin header, 1 pin [form="♂ (male)"]
  J2 = male pin header, 1 pin [form="♂ (male)"]
  J2_2 = male pin header, 1 pin [form="♂ (male)"]
  J1 = male pin header, 1 pin [form="♂ (male)"]
  J1_2 = male pin header, 1 pin [form="♂ (male)"]
  J1_3 = male pin header, 1 pin [form="♂ (male)"]
  J1_4 = male pin header, 1 pin [form="♂ (male)"]
  J2_3 = male pin header, 1 pin [form="♂ (male)"]
  J2_4 = male pin header, 1 pin [form="♂ (male)"]
  C5 = Ceramic Capacitor [capacitance="100 nF" voltage=35V package="0603 [SMD, multilayer]"]
  C9 = Ceramic Capacitor [capacitance="100 nF" voltage=35V package="0603 [SMD, multilayer]"]
  C10 = Ceramic Capacitor [capacitance="100 nF" voltage=35V package="0603 [SMD, multilayer]"]
  C6 = Ceramic Capacitor [capacitance="100 nF" voltage=35V package="0603 [SMD, multilayer]"]
  C8 = Ceramic Capacitor [capacitance="100 nF" voltage=35V package="0603 [SMD, multilayer]"]
  C7 = Ceramic Capacitor [capacitance="100 nF" voltage=35V package="0603 [SMD, multilayer]"]
  U8 = ISL43210IHZ-T7A [package=sot-23-6]
  U6 = ISL43210IHZ-T7A [package=sot-23-6]
  U7 = ISL43210IHZ-T7A [package=sot-23-6]
  U5 = ISL43210IHZ-T7A [package=sot-23-6]
  U4 = ISL43210IHZ-T7A [package=sot-23-6]
  U3 = ISL43210IHZ-T7A [package=sot-23-6]
  C1 = Ceramic Capacitor [capacitance=10µF voltage=16V package="0805 [SMD, multilayer]"]
  C2 = Ceramic Capacitor [capacitance=22µF voltage=16V package="0805 [SMD, multilayer]"]
  J6 = male pin header, 2 pins [form="♂ (male)"]
  J7 = screw terminal, 2 pins
  R15 = Resistor [tolerance=±5% resistance=1k power=0.25 package="0603 [SMD]"]

nets:
  N1: J5.pin1, U8.S, U7.S, U5.S, U4.S
  N2: J5.pin2, U6.S, U3.S
  N3: J5.pin3, R14.Pin_1
  GND: J5.pin4, Q1.source, U1.GND, C3.1, R13.Pin_1, C5.1, C9.1, C10.1, C6.1, C8.1, C7.1, U8.GND, U6.GND, U7.GND, U5.GND, U4.GND, U3.GND
  VDD: J5.pin5, U1.IN, C5.0, C9.0, C10.0, C6.0, C8.0, C7.0, U8.VDD, U6.VDD, U7.VDD, U5.VDD, U4.VDD, U3.VDD
  N4: RL1.pin1, Q1.drain, D1.anode, C4.1
  N5: RL1.pin2, J4.pin1, J4_2.pin1, J4_3.pin1, J4_4.pin1
  N6: RL1.pin4, U2.IN, C1.1
  N7: RL1.pin5, J6.pin1
  N8: RL1.pin7, J7.pin2
  N9: RL1.pin8, D1.cathode, C4.0
  N10: Q1.gate, R14.Pin_0
  N11: U1.OUT, C3.0, R13.Pin_0
  N12: U2.ADJ, U3.COM
  N13: U2.OUT, J1.pin1, J1_2.pin1, J1_3.pin1, J1_4.pin1, U6.COM, C2.1
  N14: R1.pin1, R5.Pin_1
  N15: R1.pin2, R6.Pin_1
  N16: R1.pin3, R2.pin3, R3.pin3, R4.pin3, J3.pin1, J3_2.pin1, J3_3.pin1, J3_4.pin1, J2.pin1, J2_2.pin1, J2_3.pin1, J2_4.pin1, C1.0, C2.0
  N17: R2.pin1, R7.Pin_1
  N18: R2.pin2, R8.Pin_1
  N19: R3.pin1, R9.Pin_1
  N20: R3.pin2, R10.Pin_1
  N21: R4.pin1, R11.Pin_1
  N22: R4.pin2, R12.Pin_1
  N23: R11.Pin_0, U4.NO
  N24: R9.Pin_0, U5.NO
  N25: R7.Pin_0, U5.NC
  N26: R5.Pin_0, U4.NC
  N27: R12.Pin_0, U8.NO
  N28: R10.Pin_0, U7.NO
  N29: R8.Pin_0, U7.NC
  N30: R6.Pin_0, U8.NC
  N31: U8.COM, U6.NO
  N32: U6.NC, U7.COM
  N33: U5.COM, U3.NC
  N34: U4.COM, U3.NO
  N35: J6.pin2, R15.Pin_1
  N36: J7.pin1, R15.Pin_0

notes:
  12v
  GND
  TT ON
  SPD SEL A
  SPD SEL B
  Turntable Power
  MTR -
  MTR +
  12v in
  Automatic Record Player
  Motor Controller Board v0.1 (Nov 2022)
  _
  16
  33
  45
  78
  COM
  45 / 33
  78 / 16
  Used for demuxes
  Strobe Comm
  STRB
  6.3v AC in
  6.3v AC

custom parts:
  DPDT Relay: DIP DPDT Relay (Double Pole Double Throw)
  Voltage Regulator - Variable: Variable DC Voltage Regulator
